# Fritzing sketch Circuito_PG02_CE4301_2025 (saved by Fritzing 0.9.9b)
breadboards: 1

parts:
  WeMos_D1_Mini1 = WeMos D1 Mini
  DFRobot_DFPlayer_Mini1 = DFRobot DFPlayer Mini [part_number=DFR0299]
  U2 = LM386 [package=dip08]
  SP1 = SPEAKER [package=pcb_mount_speaker]  # not connected
  M1 = DC Motor
  Q1 = NPN-Transistor [package="TO92 [THT]"]
  D1 = Rectifier Diode [part_number=1N4001 package="Melf DO-213 AB [SMD]"]
  R1 = Resistor [tolerance=±5% resistance=10k package=THT]
  S1 = Toggle Switch [package=THT]
  VCC1 = Battery
  Load_Cell1 = Load Cell - Red/white/black/green
  Componente1 = HX711 Weighing Sensor Module
  S2 = Pushbutton [package=THT]
  J1 = Basic Servo
  R2 = Resistor [tolerance=±5% resistance=1k package=THT]
  R3 = Resistor [tolerance=±5% resistance=10k package=THT]

nets:
  VCC: WeMos_D1_Mini1.5V, DFRobot_DFPlayer_Mini1.VCC, M1.pin_2, D1.cathode, S1.COM, Componente1.VCC, S2.leg1, J1.vcc
  N1: WeMos_D1_Mini1.D1, DFRobot_DFPlayer_Mini1.RX
  N2: WeMos_D1_Mini1.D2, DFRobot_DFPlayer_Mini1.TX
  N3: WeMos_D1_Mini1.D4, J1.pulse
  N4: WeMos_D1_Mini1.D5, Componente1.DO/RX
  N5: WeMos_D1_Mini1.D6, Componente1.CK/TX
  N6: WeMos_D1_Mini1.D7, R1.Pin_0, S2.leg0
  N7: WeMos_D1_Mini1.D8, R2.Pin_0
  GND: WeMos_D1_Mini1.G, DFRobot_DFPlayer_Mini1.GND-1, DFRobot_DFPlayer_Mini1.GND-2, Q1.E, R1.Pin_1, VCC1.-, Componente1.GND, J1.gnd, R3.Pin_0
  N8: DFRobot_DFPlayer_Mini1.DAC_R, U2.+IN
  N9: M1.pin_1, Q1.C, D1.anode
  N10: Q1.B, R2.Pin_1, R3.Pin_1
  N11: S1.L1, VCC1.+
  N12: Load_Cell1.wire1, Componente1.E+
  N13: Load_Cell1.wire2, Componente1.A-
  N14: Load_Cell1.wire3, Componente1.E-
  N15: Load_Cell1.wire4, Componente1.A+

custom parts:
  WeMos D1 Mini: The D1 mini is a mini wifi board based on ESP-8266EX.
  Load Cell - Red/white/black/green: A rectangle load cell/weighting pressure Sensor with four wires - Red, white, black, green. Normally corresponding with E+, E-, A+, A- respectively.
  HX711 Weighing Sensor Module: HX711 is a precision 24-bit analog-to-digital converter (ADC) designed for weigh scales and industrial control applications to interface directly with a bridge sensor.
